# Fritzing sketch Untitled Sketch 2 (saved by Fritzing 0.9.3b)
breadboards: 1

parts:
  J2 = Basic Servo
  J3 = Basic Servo
  R1 = Rotary Potentiometer (Small) [maximum_resistance=100kΩ package=THT]
  R2 = Rotary Potentiometer (Small) [maximum_resistance=100kΩ package=THT]
  R3 = Rotary Potentiometer (Small) [maximum_resistance=100kΩ package=THT]
  S1 = Pushbutton [package="[THT]"]
  btn2 = Pushbutton [package="[THT]"]
  btn1 = Pushbutton [package="[THT]"]
  LED1 = LED - 5mm [color="Red (633nm)" package="5 mm [THT]"]
  Part1 = Arduino Uno (Rev3)
  R4 = Resistor [tolerance=±5% resistance=220 package=THT]
  R5 = Resistor [tolerance=±5% resistance=220 package=THT]
  R6 = Resistor [tolerance=±5% resistance=220 package=THT]
  R7 = Resistor [tolerance=±5% resistance=220 package=THT]
  J4 = Basic Servo
  VCC1 = Battery

nets:
  GND: J2.gnd, J3.gnd, J4.gnd, VCC1.-
  VCC: J2.vcc, J3.vcc, J4.vcc, VCC1.+
  N1: J2.pulse, Part1.D6_PWM
  N2: J3.pulse, Part1.D9_PWM
  N3: R1.leg1, R2.leg1, R3.leg1, S1.Pin_1, S1.Pin_2, btn2.Pin_1, btn2.Pin_2, btn1.Pin_1, btn1.Pin_2, Part1.5V
  N4: R1.wiper, Part1.A0
  N5: R1.leg2, R2.leg2, R3.leg2, Part1.GND, R4.Pin_1, R5.Pin_1, R6.Pin_1, R7.Pin_1
  N6: R2.wiper, Part1.A1
  N7: R3.wiper, Part1.A2
  N8: S1.Pin_3, S1.Pin_4, Part1.D8, R4.Pin_0
  N9: btn2.Pin_3, btn2.Pin_4, Part1.D13/SCK, R5.Pin_0
  N10: btn1.Pin_3, btn1.Pin_4, Part1.D12/MISO, R6.Pin_0
  N11: LED1.cathode, Part1.D2
  N12: LED1.anode, R7.Pin_0
  N13: Part1.D7, J4.pulse
